# Fritzing sketch track_the_led_fly (saved by Fritzing 0.9.3b)
breadboards: 1

parts:
  Part1 = Arduino Uno (Rev3)
  LED2 = LED - 5mm [color="Green (555nm)" package="5 mm [THT]"]
  LED3 = LED - 5mm [color="Green (555nm)" package="5 mm [THT]"]
  LED4 = LED - 5mm [color="Green (555nm)" package="5 mm [THT]"]
  LED5 = LED - 5mm [color="Red (633nm)" package="5 mm [THT]"]
  LED6 = LED - 5mm [color="Green (555nm)" package="5 mm [THT]"]
  S1 = Pushbutton [package="[THT]"]
  S2 = Pushbutton [package="[THT]"]
  S3 = Pushbutton [package="[THT]"]
  S4 = Pushbutton [package="[THT]"]
  R1 = Rotary Potentiometer (Small) [maximum_resistance=100kΩ package=THT]
  R2 = Resistor [tolerance=±5% resistance=220 package="0603 [SMD]"]
  R3 = Resistor [tolerance=±5% resistance=220 package="0603 [SMD]"]
  R4 = Resistor [tolerance=±5% resistance=220 package="0603 [SMD]"]
  R5 = Resistor [tolerance=±5% resistance=220 package="0603 [SMD]"]
  R6 = Resistor [tolerance=±5% resistance=220 package="0603 [SMD]"]

nets:
  N1: Part1.A5/SCL, R1.wiper
  N2: Part1.D8, R4.Pin_1
  N3: Part1.D9_PWM, R5.Pin_1
  N4: Part1.D11_PWM/MOSI, R6.Pin_1
  N5: Part1.D2, S1.Pin_3, S1.Pin_4
  N6: Part1.D3_PWM, S2.Pin_3, S2.Pin_4
  N7: Part1.D4, S3.Pin_3, S3.Pin_4
  N8: Part1.D5_PWM, S4.Pin_3, S4.Pin_4
  N9: Part1.D6_PWM, R2.Pin_1
  N10: Part1.D7, R3.Pin_1
  N11: Part1.5V, R1.leg1
  N12: Part1.GND, LED2.cathode, LED3.cathode, LED4.cathode, LED5.cathode, LED6.cathode, S1.Pin_1, S1.Pin_2, S2.Pin_1, S2.Pin_2, S3.Pin_1, S3.Pin_2, S4.Pin_1, S4.Pin_2, R1.leg2
  N13: LED2.anode, R3.Pin_0
  N14: LED4.anode, R5.Pin_0
  N15: LED5.anode, R6.Pin_0
  N16: LED6.anode, R2.Pin_0
